# Fritzing sketch Water_flow_sensor_MQTT (saved by Fritzing 0.9.3b)

parts:
  WeMos_D1_Mini1 = WeMos D1 Mini
  YF-S201_Flow_Meter1 = YF-S201 Water Flow Meter

nets:
  5V: WeMos_D1_Mini1.5V, YF-S201_Flow_Meter1.VCC
  N1: WeMos_D1_Mini1.D2, YF-S201_Flow_Meter1.GND
  N2: WeMos_D1_Mini1.G, YF-S201_Flow_Meter1.SIG

custom parts:
  WeMos D1 Mini: The D1 mini is a mini wifi board based on ESP-8266EX.
  YF-S201 Water Flow Meter: The YF-S201 Flow Meter. The input voltage is 5V to 24V (DC).
